# Fritzing sketch mega (saved by Fritzing 0.9.0b)
breadboards: 1

parts:
  Part1 = Arduino Mega 2560 (Rev3)
  NRF24L2 = NRF24L01
  C3 = Capacitor Polarized [package=cpol-radial-10uf-25v]

nets:
  3V3: Part1.3V3, NRF24L2.VCC, C3.+
  GND: Part1.GND, NRF24L2.GND, C3.-
  N1: Part1.D40, NRF24L2.CE
  N2: Part1.D50, NRF24L2.MISO
  N3: Part1.D51, Part1.D53, NRF24L2.MOSI
  N4: Part1.D52, NRF24L2.SCK

custom parts:
  NRF24L01: NRF24L01 module
